# Fritzing sketch robot circuit (saved by Fritzing 0.9.3b)
circuit board: 8.46667cm x 5.64444cm

parts:
  Part2 = Arduino Nano (Rev3.0) (ICSP)
  J2 = Basic Servo
  J3 = Basic Servo
  M1 = RioRand LM2596
  Mod1 = KY-019 5V Relay Module [package="Breakout board"]
  J4 = Basic Servo

nets:
  N1: Part2.D2, J2.pulse
  N2: Part2.D3, J4.pulse
  N3: Part2.D4, J3.pulse
  N4: Part2.D5, Mod1.S
  N5: Part2.GND, Mod1.-
  N6: Part2.5V, Mod1.+
  GND: J2.gnd, J3.gnd, M1.Pin_4, J4.gnd
  VCC: J2.vcc, J3.vcc, M1.Pin_3, J4.vcc

custom parts:
  KY-019 5V Relay Module: KY-019 5V Relay module, used to control AC circuits. (Special thanks to vanepp for fixing the PCB holes and other errors)
